# Fritzing sketch linorobot_2wdrev2 (saved by Fritzing 0.9.3b)

parts:
  S2 = H-Bridge with L298N
  Part1 = GY-80
  Teensy_3_1 = Teensy 3.0 [part_number="Freescale ARM MK20DX128"]
  S3 = H-Bridge with L298N
  M2 = DC Motor
  M1 = DC Motor
  J1 = female pin header, 4 pins [form="♀ (female)"]
  J2 = female pin header, 4 pins [form="♀ (female)"]
  J3 = female pin header, 2 pins [form="♀ (female)"]
  J4 = female pin header, 2 pins [form="♀ (female)"]

nets:
  N1: S2.12V, J3.pin2
  N2: S2.GND, J1.pin1, J4.pin1
  N3: S2.5V, J1.pin4
  N4: S2.ENA, Teensy_3_1.21
  N5: S2.IN1, Teensy_3_1.20
  N6: S2.IN2, Teensy_3_1.1
  N7: S2.M1-01, M1.pin_2
  N8: S2.M1-02, M1.pin_1
  N9: Part1.VCC_3.3V, Teensy_3_1.3.3V
  GND: Part1.GND, Teensy_3_1.GND, S3.GND, J2.pin1, J4.pin2
  N10: Part1.SCL, Teensy_3_1.19
  N11: Part1.SDA, Teensy_3_1.18
  N12: Teensy_3_1.15, J1.pin3
  N13: Teensy_3_1.14, J1.pin2
  N14: Teensy_3_1.5, S3.ENB
  N15: Teensy_3_1.6, S3.IN3
  N16: Teensy_3_1.8, S3.IN4
  N17: Teensy_3_1.11, J2.pin2
  N18: Teensy_3_1.12, J2.pin3
  N19: S3.12V, J3.pin1
  N20: S3.5V, J2.pin4
  N21: S3.M2-01, M2.pin_1
  N22: S3.M2-02, M2.pin_2

notes:
  GND
  B
  A
  5V
  +
  -
  12V BATTERY
  MOTOR1
  MOTOR2
  ENCODER1
  ENCODER2
  ENCODER3

custom parts:
  H-Bridge with L298N: h-bridge
