# Fritzing sketch linorobot_4wdrev2 (saved by Fritzing 0.9.3b)

parts:
  S2 = H-Bridge with L298N
  Part1 = GY-80
  Teensy_3_1 = Teensy 3.0 [part_number="Freescale ARM MK20DX128"]
  S3 = H-Bridge with L298N
  M2 = DC Motor
  M1 = DC Motor
  J1 = female pin header, 4 pins [form="♀ (female)"]
  J2 = female pin header, 4 pins [form="♀ (female)"]
  J3 = female pin header, 2 pins [form="♀ (female)"]
  J4 = female pin header, 2 pins [form="♀ (female)"]
  S4 = H-Bridge with L298N
  S5 = H-Bridge with L298N
  M3 = DC Motor
  M4 = DC Motor
  J5 = female pin header, 4 pins [form="♀ (female)"]
  J6 = female pin header, 4 pins [form="♀ (female)"]

nets:
  12V: S2.12V, J3.pin2, S4.12V, S5.12V
  N1: S2.GND, J1.pin1, J4.pin1
  N2: S2.5V, J1.pin4
  N3: S2.ENA, Teensy_3_1.21
  N4: S2.IN1, Teensy_3_1.20
  N5: S2.IN2, Teensy_3_1.1
  N6: S2.M1-01, M1.pin_2
  N7: S2.M1-02, M1.pin_1
  N8: Part1.VCC_3.3V, Teensy_3_1.3.3V
  GND: Part1.GND, Teensy_3_1.GND, S3.GND, J2.pin1, J4.pin2, S4.GND, S5.GND, J5.pin4, J6.pin4
  N9: Part1.SCL, Teensy_3_1.19
  N10: Part1.SDA, Teensy_3_1.18
  N11: Teensy_3_1.23, S5.IN4
  N12: Teensy_3_1.22, S5.ENB
  N13: Teensy_3_1.17, J5.pin2
  N14: Teensy_3_1.16, J5.pin3
  N15: Teensy_3_1.15, J1.pin3
  N16: Teensy_3_1.14, J1.pin2
  N17: Teensy_3_1.0, S5.IN3
  N18: Teensy_3_1.2, S4.IN1
  N19: Teensy_3_1.3, S4.IN2
  N20: Teensy_3_1.4, S4.ENA
  N21: Teensy_3_1.5, S3.ENB
  N22: Teensy_3_1.6, S3.IN3
  N23: Teensy_3_1.8, S3.IN4
  N24: Teensy_3_1.9, J6.pin3
  N25: Teensy_3_1.10, J6.pin2
  N26: Teensy_3_1.11, J2.pin2
  N27: Teensy_3_1.12, J2.pin3
  N28: S3.12V, J3.pin1
  N29: S3.5V, J2.pin4
  N30: S3.M2-01, M2.pin_1
  N31: S3.M2-02, M2.pin_2
  N32: S4.5V, J6.pin1
  N33: S4.M1-01, M4.pin_2
  N34: S4.M1-02, M4.pin_1
  N35: S5.5V, J5.pin1
  N36: S5.M2-01, M3.pin_1
  N37: S5.M2-02, M3.pin_2

notes:
  GND
  B
  A
  5V
  +
  -
  12V BATTERY
  MOTOR1
  MOTOR2
  ENCODER1
  ENCODER2
  MOTOR3
  MOTOR4
  ENCODER3
  ENCODER4

custom parts:
  H-Bridge with L298N: h-bridge
